// Digital circuit DWAK2.dig as structural Verilog
module DWAK2 (
  input  clk
);

  wire comparator_1_eq, not_1_out, register_1_q;
  wire [9:0] counter_1_out;
  wire [63:0] Program_ROM_d;

  EEPROMDualPort #(.AddrBits(10), .Bits(64)) Program_ROM (
    .A(counter_1_out), .Din({64{1'b0}}), .str(1'b0), .C(clk), .ld(1'b1), .D(Program_ROM_d));
  Counter #(.Bits(10)) counter_1 (.en(1'b1), .C(clk), .clr(1'b0), .out(counter_1_out));  // open: ovf
  Comparator #(.Bits(10)) comparator_1 (.a(counter_1_out), .b({10{1'b1}}), .eq(comparator_1_eq));  // open: gt, lt
  Register register_1 (.D(1'b1), .C(comparator_1_eq), .en(not_1_out), .Q(register_1_q));
  not not_1 (not_1_out, register_1_q);
  ram ram_1 (
    .addr_read1({64{1'b0}}), .addr_read2(64'h1), .addr_write({{54{1'b0}}, counter_1_out}),
    .data_write(Program_ROM_d), .store_write(not_1_out), .clock(clk));  // open: res_read1, res_read2

  // Notes on the sheet:
  //   clk: Hz: 50
  //   contents of Program_ROM (hex, n*v repeats v):
  //   cafebabe,deadb0b
endmodule
