// Digital circuit fetcher.dig as structural Verilog
module fetcher (
  input  [63:0] IP,
  input  [63:0] word1,
  input  clock,
  output [7:0] IP_read,
  output [63:0] ram_addr
);

  wire comparator_1_eq;
  wire [2:0] counter_1_out;

  Counter #(.Bits(3)) counter_1 (.en(1'b1), .C(clock), .clr(comparator_1_eq), .out(counter_1_out));  // open: ovf
  Comparator #(.Bits(3)) comparator_1 (.a(word1[2:0]), .b(counter_1_out), .eq(comparator_1_eq));  // open: gt, lt

  assign IP_read = {8{1'b1}};
  assign ram_addr = IP;
endmodule
